# Fritzing sketch adc-light-sensor (saved by Fritzing 0.9.3b)
breadboards: 1

parts:
  U2 = ESP 32 DEVKIT DOIT
  R1 = Resistor [tolerance=±5% resistance=10k package=THT]
  R2 = Photocell (LDR) [package=THT]

nets:
  N1: U2.D22, U2.D4, U2.3V3, R2.pin_1
  N2: U2.GND, R1.Pin_1
  N3: U2.D13, U2.D14
  N4: U2.D27, R1.Pin_0, R2.pin_0
