# Fritzing sketch button-interrupt (saved by Fritzing 0.9.3b)
breadboards: 1

parts:
  U2 = ESP 32 DEVKIT DOIT
  LED1 = LED - 5mm [color="Red (633nm)" package="5 mm [THT]"]
  LED2 = LED - 5mm [color="Green (555nm)" package="5 mm [THT]"]
  R3 = Resistor [tolerance=±5% resistance=100 package=THT]
  R4 = Resistor [tolerance=±5% resistance=100 package=THT]
  S1 = Pushbutton [package="[THT]"]

nets:
  N1: U2.D22, U2.3V3, LED1.cathode, LED2.cathode
  N2: U2.GND, S1.Pin_1, S1.Pin_2
  N3: U2.D13, U2.D14
  N4: U2.D12, S1.Pin_3, S1.Pin_4
  N5: U2.D26, R4.Pin_1
  N6: U2.D25, R3.Pin_1
  N7: LED1.anode, R3.Pin_0
  N8: LED2.anode, R4.Pin_0
