# Fritzing sketch serial-led-control (saved by Fritzing 0.9.3b)
breadboards: 1

parts:
  U2 = ESP 32 DEVKIT DOIT
  LED1 = LED - 5mm [color="Red (633nm)" package="5 mm [THT]"]
  R3 = Resistor [tolerance=±5% resistance=100 package=THT]

nets:
  N1: U2.D22, U2.3V3, LED1.cathode
  N2: U2.D13, U2.D14
  N3: U2.D25, R3.Pin_1
  N4: LED1.anode, R3.Pin_0
